# Fritzing sketch ESP8266-DHT12 (saved by Fritzing 0.9.10b)
breadboards: 1

parts:
  Mod1 = Amica NodeMCU DEVKIT 1.0
  DHT1 = DHT12 Humitidy and Temperature Sensor I2C.
  R1 = Resistor [tolerance=±5% resistance=4.7k package=THT]

nets:
  N1: Mod1.pin1, Mod1.pin_10, Mod1.pin_26, DHT1.SCL
  N2: Mod1.pin2, Mod1.pin_9, Mod1.pin_25, Mod1.pin_29, DHT1.VDD, R1.Pin_0
  N3: Mod1.pin_13, DHT1.SDA, R1.Pin_1

custom parts:
  DHT12 Humitidy and Temperature Sensor I2C.: DHT12 Humidity and Temperature Sensor I2C. Supply voltage: 2.7V to 5.5V Current: Standby 30uA, Active 800uA Temperature: -20ºC to 60ºC, res. 0.1ºC Humidity: 20%RH to 95%RH, res. 0.1%RH ID I2C 0x5c

// code stored in the sketch: ESP8266-DHT12.ino
#include "DHT.h"
#define DHTPIN D2
#define DHTTYPE DHT11

DHT dht11(DHTPIN, DHTTYPE);

void setup() {
  Serial.begin(115200);
  dht11.begin();
}

void loop() {
  delay(5000);

  int humi = dht11.readHumidity() * 10;
  int temp = dht11.readTemperature() * 10;
  if(temp < 0)    // if temperature < 0
    Serial.printf("Temp: -%02u.%1u°C\n", (abs(temp)/10)%100, abs(temp) % 10);
  else            // temperature >= 0
    Serial.printf("Temp: %02u.%1u°C\n", (temp/10)%100, temp % 10);

  Serial.printf("Humi: %02u.%1u%%\n", (humi/10)%100, humi % 10);
}
